// Logisim project LFSR.circ as structural Verilog: 1 circuit, main circuit LFSR
module LFSR (
  output out_1
);

  wire button_1_out, shift_register_1_p2, shift_register_1_p4, shift_register_1_p5;

  Button button_1 (.out(button_1_out));
  // Probe on shift_register_1_p2
  // Shift_Register #(.length(16)) shift_register_1: pin names not known; wires that end beside it: 1'b1, shift_register_1_p2, button_1_out, shift_register_1_p4, shift_register_1_p5, out_1
  xor xor_1 (shift_register_1_p2, shift_register_1_p4, shift_register_1_p5);
endmodule
